// Logisim project 74_series_computer_schematic.circ as structural Verilog: 10 circuits, main circuit main
module main (
  input  in_1,
  input  in_2,
  input  in_3,
  input  in_4,
  input  in_5,
  input  in_6,
  input  in_7,
  input  in_8,
  input  in_9,
  input  in_10,
  input  in_11,
  input  in_12,
  input  in_13,
  input  in_14,
  input  in_15,
  input  in_16,
  input  in_17,
  input  in_18,
  input  in_19,
  input  in_20
);

  wire ALU_carry_out, button_1_out, button_2_out, button_3_out, button_4_out, button_5_out, button_6_out,
       button_7_out, button_8_out, CLOCK_clock_out, USER_INPUT_waiting_for_user, ZERO_CHECK_is_zero;
  wire [7:0] A_REGISTER_content, ALU_unbuffered_result, B_REGISTER_content, MEMORY_ADDRESS_REGISTER_content,
       USER_INPUT_buffered_output;

  // Probe on USER_INPUT_waiting_for_user
  // Probe on ALU_carry_out
  // Probe on ZERO_CHECK_is_zero
  Button button_1 (.out(button_1_out));
  Button button_2 (.out(button_2_out));
  Button button_3 (.out(button_3_out));
  Button button_4 (.out(button_4_out));
  Button button_5 (.out(button_5_out));
  Button button_6 (.out(button_6_out));
  Button button_7 (.out(button_7_out));
  Button button_8 (.out(button_8_out));
  user_input USER_INPUT (
    .user_finished(button_2_out), .start_user_wait(in_4), .buffered_output(USER_INPUT_buffered_output),
    .waiting_for_user(USER_INPUT_waiting_for_user), .clear(button_3_out), .output_enable(in_3));  // open: user_input
  clock CLOCK (.manual_clock(button_1_out), .clock_out(CLOCK_clock_out), .auto_manual_step(in_1), .halt(in_2));
  program_counter PROGRAM_COUNTER (
    .buffered_input(USER_INPUT_buffered_output), .increment(in_7), .clock(CLOCK_clock_out),
    .clear(button_4_out), .output_enable(in_6), .buffered_output(USER_INPUT_buffered_output), .load(in_5));
  regsiter A_REGISTER (
    .buffered_input(USER_INPUT_buffered_output), .buffered_output(USER_INPUT_buffered_output),
    .content(A_REGISTER_content), .input_enable(in_8), .clock(CLOCK_clock_out), .clear(button_5_out),
    .output_enable(in_9));
  alu ALU (
    .add_sub(in_10), .buffered_result(USER_INPUT_buffered_output), .A_input(A_REGISTER_content),
    .output_enable(in_11), .B_input(B_REGISTER_content), .carry_out(ALU_carry_out),
    .unbuffered_result(ALU_unbuffered_result));
  regsiter B_REGISTER (
    .buffered_input(USER_INPUT_buffered_output), .buffered_output(USER_INPUT_buffered_output),
    .content(B_REGISTER_content), .input_enable(in_12), .clock(CLOCK_clock_out), .clear(button_6_out),
    .output_enable(in_13));
  zero_check ZERO_CHECK (
    .buffered_input(USER_INPUT_buffered_output), .is_zero(ZERO_CHECK_is_zero), .input_enable(in_14));
  regsiter MEMORY_ADDRESS_REGISTER (
    .buffered_input(USER_INPUT_buffered_output), .content(MEMORY_ADDRESS_REGISTER_content),
    .input_enable(in_15), .clock(CLOCK_clock_out), .clear(button_7_out), .output_enable(in_16));  // open: buffered_output
  RAM RAM (
    .input_enable(in_17), .address(MEMORY_ADDRESS_REGISTER_content), .output_enable(in_18),
    .buffered_input(USER_INPUT_buffered_output), .clock(CLOCK_clock_out),
    .buffered_output(USER_INPUT_buffered_output));
  regsiter INSTRUCTION_REGISTER (
    .buffered_input(USER_INPUT_buffered_output), .input_enable(in_19), .clock(CLOCK_clock_out),
    .clear(button_8_out), .output_enable(in_20));  // open: buffered_output, content
  // Probe on A_REGISTER_content
  // Probe on ALU_unbuffered_result
  // Probe on B_REGISTER_content
endmodule

module alu (
  input  [7:0] A_input,
  input  output_enable,
  input  add_sub,
  input  [7:0] B_input,
  output [7:0] buffered_result,
  output carry_out,
  output [7:0] unbuffered_result
);

  wire [7:0] xor_1_out;

  assign xor_1_out = {8{add_sub}} ^ B_input;  // XOR_Gate xor_1, 8 bits wide
  Adder adder_1 (.a(A_input), .b(xor_1_out), .out(unbuffered_result), .cin(add_sub), .cout(carry_out));
  assign buffered_result = output_enable ? unbuffered_result : 8'bz;  // Controlled_Buffer controlled_buffer_1
endmodule

module regsiter (
  input  [7:0] buffered_input,
  input  input_enable,
  input  clock,
  input  clear,
  input  output_enable,
  output [7:0] content,
  output [7:0] buffered_output
);

  wire and_1_out;
  wire [7:0] controlled_buffer_1_out;

  assign controlled_buffer_1_out = input_enable ? buffered_input : 8'bz;  // Controlled_Buffer controlled_buffer_1
  Register register_1 (.D(controlled_buffer_1_out), .en(1'b1), .Q(content), .clk(and_1_out), .clr(clear));
  and and_1 (and_1_out, input_enable, clock);
  assign buffered_output = output_enable ? content : 8'bz;  // Controlled_Buffer controlled_buffer_2
endmodule

module clock (
  input  manual_clock,
  input  auto_manual_step,
  input  halt,
  output clock_out
);

  wire auto_clock_out, multiplexer_1_out, not_1_out;

  Clock auto_clock (.out(auto_clock_out));
  Multiplexer multiplexer_1 (
    .in0(auto_clock_out), .in1(manual_clock), .out(multiplexer_1_out), .sel(auto_manual_step), .en(1'b1));
  not not_1 (not_1_out, halt);
  and and_1 (clock_out, multiplexer_1_out, not_1_out);
endmodule

module RAM (
  input  [7:0] buffered_input,
  input  input_enable,
  input  [7:0] address,
  input  clock,
  input  output_enable,
  output [7:0] buffered_output
);

  wire not_1_out;
  wire [7:0] ram_1_data;

  RAM_part ram_1 (.addr(address), .data(ram_1_data), .sel(1'b1), .clk(clock), .ld(not_1_out), .clr(1'b0));
  not not_1 (not_1_out, input_enable);
  assign ram_1_data = input_enable ? buffered_input : 8'bz;  // Controlled_Buffer controlled_buffer_1
  assign buffered_output = output_enable ? ram_1_data : 8'bz;  // Controlled_Buffer controlled_buffer_2
endmodule

module program_counter (
  input  load,
  input  output_enable,
  input  [7:0] buffered_input,
  input  increment,
  input  clock,
  input  clear,
  output [7:0] buffered_output
);

  wire [7:0] controlled_buffer_1_out, counter_1_q;

  assign controlled_buffer_1_out = load ? buffered_input : 8'bz;  // Controlled_Buffer controlled_buffer_1
  Counter counter_1 (
    .load(load), .D(controlled_buffer_1_out), .count(increment), .Q(counter_1_q), .clk(clock), .clr(clear));  // open: carry
  assign buffered_output = output_enable ? counter_1_q : 8'bz;  // Controlled_Buffer controlled_buffer_2
endmodule

module user_input (
  input  output_enable,
  input  [7:0] user_input,
  input  user_finished,
  input  start_user_wait,
  input  clear,
  output [7:0] buffered_output,
  output waiting_for_user
);

  wire and_1_out, or_1_out;

  and and_1 (and_1_out, waiting_for_user, user_finished);
  assign buffered_output = output_enable ? user_input : 8'bz;  // Controlled_Buffer controlled_buffer_1
  or or_1 (or_1_out, and_1_out, start_user_wait);
  J_K_Flip_Flop j_k_ff_1 (
    .J(1'b1), .clk(or_1_out), .K(1'b1), .Q(waiting_for_user), .preset(1'b0), .en(1'b1), .reset(clear));  // open: Qn
endmodule

module instruction_decoder (
  output user_input_output_enable,
  output user_input_start_user_wait,
  output user_input_waiting_for_user,
  output program_counter_output_enable,
  output program_counter_load,
  output program_counter_increment,
  output register_A_input_enable,
  output register_A_output_enable,
  output alu_output_enable,
  output alu_add_sub,
  output alu_overflow,
  output register_B_input_enable,
  output register_B_output_enable,
  output zero_check_is_zero,
  output output_register_input_enable,
  output memory_address_register_input_enable,
  output ram_input_enable,
  output ram_output_enable,
  output instruction_register_input_enable
);
endmodule

module zero_check (
  input  [7:0] buffered_input,
  input  input_enable,
  output is_zero
);

  wire [7:0] controlled_buffer_1_out;

  assign controlled_buffer_1_out = input_enable ? buffered_input : 8'bz;  // Controlled_Buffer controlled_buffer_1
  Pull_Resistor #(.pull(1)) pull_resistor_1 (.node(controlled_buffer_1_out[0]));
  Pull_Resistor #(.pull(1)) pull_resistor_2 (.node(controlled_buffer_1_out[3]));
  Pull_Resistor #(.pull(1)) pull_resistor_3 (.node(controlled_buffer_1_out[2]));
  Pull_Resistor #(.pull(1)) pull_resistor_4 (.node(controlled_buffer_1_out[1]));
  Pull_Resistor #(.pull(1)) pull_resistor_5 (.node(controlled_buffer_1_out[4]));
  Pull_Resistor #(.pull(1)) pull_resistor_6 (.node(controlled_buffer_1_out[7]));
  Pull_Resistor #(.pull(1)) pull_resistor_7 (.node(controlled_buffer_1_out[5]));
  Pull_Resistor #(.pull(1)) pull_resistor_8 (.node(controlled_buffer_1_out[6]));
  nor nor_1 (is_zero, controlled_buffer_1_out[0], controlled_buffer_1_out[1], controlled_buffer_1_out[2], controlled_buffer_1_out[3], controlled_buffer_1_out[4], controlled_buffer_1_out[5], controlled_buffer_1_out[6], controlled_buffer_1_out[7]);
endmodule

module subtraction_test (
  input  in_1,
  input  [7:0] in_2,
  input  in_3,
  input  [7:0] in_4,
  input  in_5,
  input  [7:0] in_6,
  input  in_7,
  input  [7:0] in_8,
  input  [7:0] A,
  input  in_10,
  input  [7:0] B,
  input  in_12,
  input  add_sub,
  output [7:0] out_14,
  output [7:0] out_15
);

  wire alu_1_carry_out, alu_2_carry_out, alu_3_carry_out;
  wire [7:0] alu_3_buffered_result, alu_4_buffered_result, multiplexer_1_out;

  LED led_1 (.in(alu_1_carry_out));
  LED led_2 (.in(alu_2_carry_out));
  LED led_3 (.in(alu_3_carry_out));
  alu alu_1 (
    .add_sub(in_1), .A_input(in_2), .output_enable(in_3), .B_input(in_4), .carry_out(alu_1_carry_out),
    .unbuffered_result(out_14));  // open: buffered_result
  alu alu_2 (
    .add_sub(in_5), .A_input(in_6), .output_enable(in_7), .B_input(in_8), .carry_out(alu_2_carry_out),
    .unbuffered_result(out_15));  // open: buffered_result
  alu alu_3 (
    .add_sub(in_10), .buffered_result(alu_3_buffered_result), .A_input(A), .output_enable(in_12),
    .B_input(multiplexer_1_out), .carry_out(alu_3_carry_out));  // open: unbuffered_result
  alu alu_4 (
    .add_sub(1'b1), .buffered_result(alu_4_buffered_result), .A_input({8{1'b0}}), .output_enable(1'b1),
    .B_input(B));  // open: carry_out, unbuffered_result
  // Probe on alu_3_buffered_result
  Multiplexer #(.width(8)) multiplexer_1 (
    .in0(B), .in1(alu_4_buffered_result), .out(multiplexer_1_out), .sel(add_sub));  // open: en
  // Probe on multiplexer_1_out
  // Probe on alu_4_buffered_result
  RAM_part ram_1 ();  // open: addr, data, sel, clk, ld, clr
endmodule
