# Fritzing sketch control_unit (saved by Fritzing 0.9.3b)
breadboards: 5

parts:
  IC1 = DIP - 28 pins [chip_label=AT28C256 package="DIP (Dual Inline) [THT]"]
  J1 = female pin header, 7 pins [form="♀ (female)"]
  J2 = female pin header, 8 pins [form="♀ (female)"]
  J3 = female pin header, 7 pins [form="♀ (female)"]
  IC2 = DIP - 28 pins [chip_label=AT28C256 package="DIP (Dual Inline) [THT]"]
  J4 = female pin header, 8 pins [form="♀ (female)"]
  J5 = female pin header, 8 pins [form="♀ (female)"]
  IC3 = 74HCT377 [chip_label=74HCT377 package="DIP (Dual Inline) [THT]"]
  J6 = female pin header, 8 pins [form="♀ (female)"]
  IC4 = DIP - 16 pins [chip_label=74HCT173 package="DIP (Dual Inline) [THT]"]
  IC5 = DIP - 14 pins [chip_label=74HCT04 package="DIP (Dual Inline) [THT]"]
  IC6 = DIP - 16 pins [chip_label=74HCT161 package="DIP (Dual Inline) [THT]"]
  LED2 = LED - 5mm [color="Green (555nm)" package="5 mm [THT]"]
  LED3 = LED - 5mm [color="Green (555nm)" package="5 mm [THT]"]
  LED4 = LED - 5mm [color="Green (555nm)" package="5 mm [THT]"]
  RESET = female pin header, 2 pins [form="♀ (female)"]
  C/U_TIMER_RESET = female pin header, 2 pins [form="♀ (female)"]
  IC7 = DIP - 16 pins [chip_label=74HCT138 package="DIP (Dual Inline) [THT]"]
  C/U_TIMER_RESET1 = female pin header, 2 pins [form="♀ (female)"]
  LED5 = LED - 5mm [color="Green (555nm)" package="5 mm [THT]"]
  LED6 = LED - 5mm [color="Green (555nm)" package="5 mm [THT]"]
  LED7 = LED - 5mm [color="Green (555nm)" package="5 mm [THT]"]
  LED8 = LED - 5mm [color="Green (555nm)" package="5 mm [THT]"]
  LED9 = LED - 5mm [color="Green (555nm)" package="5 mm [THT]"]
  LED10 = LED - 5mm [color="Green (555nm)" package="5 mm [THT]"]
  LED11 = LED - 5mm [color="Green (555nm)" package="5 mm [THT]"]
  LED12 = LED - 5mm [color="Green (555nm)" package="5 mm [THT]"]
  LED13 = LED - 5mm [color="Green (555nm)" package="5 mm [THT]"]
  LED14 = LED - 5mm [color="Green (555nm)" package="5 mm [THT]"]
  LED15 = LED - 5mm [color="Green (555nm)" package="5 mm [THT]"]
  LED16 = LED - 5mm [color="Green (555nm)" package="5 mm [THT]"]
  LED17 = LED - 5mm [color="Green (555nm)" package="5 mm [THT]"]
  LED18 = LED - 5mm [color="Green (555nm)" package="5 mm [THT]"]
  LED19 = LED - 5mm [color="Green (555nm)" package="5 mm [THT]"]
  LED20 = LED - 5mm [color="Green (555nm)" package="5 mm [THT]"]
  LED21 = LED - 5mm [color="Green (555nm)" package="5 mm [THT]"]
  LED22 = LED - 5mm [color="Green (555nm)" package="5 mm [THT]"]
  LED23 = LED - 5mm [color="Green (555nm)" package="5 mm [THT]"]
  LED24 = LED - 5mm [color="Green (555nm)" package="5 mm [THT]"]
  J7 = female pin header, 8 pins [form="♀ (female)"]
  J8 = female pin header, 4 pins [form="♀ (female)"]
  IC8 = DIP - 28 pins [chip_label=AT28C256 package="DIP (Dual Inline) [THT]"]
  J9 = female pin header, 7 pins [form="♀ (female)"]
  J10 = female pin header, 7 pins [form="♀ (female)"]
  J11 = female pin header, 8 pins [form="♀ (female)"]
  J12 = female pin header, 8 pins [form="♀ (female)"]
  IC9 = DIP - 28 pins [chip_label=AT28C256 package="DIP (Dual Inline) [THT]"]
  LED25 = LED - 5mm [color="Yellow (585nm)" package="5 mm [THT]"]  # not connected
  LED26 = LED - 5mm [color="Yellow (585nm)" package="5 mm [THT]"]  # not connected
  LED27 = LED - 5mm [color="Yellow (585nm)" package="5 mm [THT]"]
  LED28 = LED - 5mm [color="Yellow (585nm)" package="5 mm [THT]"]
  LED29 = LED - 5mm [color="Yellow (585nm)" package="5 mm [THT]"]
  LED30 = LED - 5mm [color="Yellow (585nm)" package="5 mm [THT]"]  # not connected
  LED31 = LED - 5mm [color="Yellow (585nm)" package="5 mm [THT]"]
  LED32 = LED - 5mm [color="Yellow (585nm)" package="5 mm [THT]"]  # not connected
  LED33 = LED - 5mm [color="Yellow (585nm)" package="5 mm [THT]"]  # not connected
  LED34 = LED - 5mm [color="Yellow (585nm)" package="5 mm [THT]"]  # not connected
  LED35 = LED - 5mm [color="Yellow (585nm)" package="5 mm [THT]"]
  LED36 = LED - 5mm [color="Yellow (585nm)" package="5 mm [THT]"]  # not connected
  LED37 = LED - 5mm [color="Yellow (585nm)" package="5 mm [THT]"]
  LED38 = LED - 5mm [color="Yellow (585nm)" package="5 mm [THT]"]
  LED39 = LED - 5mm [color="Yellow (585nm)" package="5 mm [THT]"]
  LED40 = LED - 5mm [color="Yellow (585nm)" package="5 mm [THT]"]  # not connected
  LED41 = LED - 5mm [color="Yellow (585nm)" package="5 mm [THT]"]  # not connected
  LED42 = LED - 5mm [color="Yellow (585nm)" package="5 mm [THT]"]  # not connected
  LED43 = LED - 5mm [color="Yellow (585nm)" package="5 mm [THT]"]
  LED44 = LED - 5mm [color="Yellow (585nm)" package="5 mm [THT]"]  # not connected
  LED45 = LED - 5mm [color="Yellow (585nm)" package="5 mm [THT]"]
  LED46 = LED - 5mm [color="Yellow (585nm)" package="5 mm [THT]"]
  LED47 = LED - 5mm [color="Yellow (585nm)" package="5 mm [THT]"]
  LED48 = LED - 5mm [color="Yellow (585nm)" package="5 mm [THT]"]  # not connected
  LED49 = LED - 5mm [color="Yellow (585nm)" package="5 mm [THT]"]  # not connected
  LED51 = LED - 5mm [color="Yellow (585nm)" package="5 mm [THT]"]
  LED53 = LED - 5mm [color="Yellow (585nm)" package="5 mm [THT]"]
  LED55 = LED - 5mm [color="Yellow (585nm)" package="5 mm [THT]"]
  LED56 = LED - 5mm [color="Yellow (585nm)" package="5 mm [THT]"]  # not connected
  J13 = female pin header, 8 pins [form="♀ (female)"]
  J14 = female pin header, 8 pins [form="♀ (female)"]
  J15 = female pin header, 8 pins [form="♀ (female)"]
  J16 = female pin header, 5 pins [form="♀ (female)"]
  R1 = Resistor [tolerance=±5% resistance=220 package=THT]
  R2 = Resistor [tolerance=±5% resistance=220 package=THT]
  R3 = Resistor [tolerance=±5% resistance=220 package=THT]
  R4 = Resistor [tolerance=±5% resistance=220 package=THT]
  R5 = Resistor [tolerance=±5% resistance=220 package=THT]
  R6 = Resistor [tolerance=±5% resistance=220 package=THT]
  R7 = Resistor [tolerance=±5% resistance=220 package=THT]
  R8 = Resistor [tolerance=±5% resistance=220 package=THT]
  R9 = Resistor [tolerance=±5% resistance=220 package=THT]
  R10 = Resistor [tolerance=±5% resistance=220 package=THT]
  R11 = Resistor [tolerance=±5% resistance=220 package=THT]
  R12 = Resistor [tolerance=±5% resistance=220 package=THT]
  R13 = Resistor [tolerance=±5% resistance=220 package=THT]
  R14 = Resistor [tolerance=±5% resistance=220 package=THT]
  R15 = Resistor [tolerance=±5% resistance=220 package=THT]
  R16 = Resistor [tolerance=±5% resistance=220 package=THT]
  R17 = Resistor [tolerance=±5% resistance=220 package=THT]
  R18 = Resistor [tolerance=±5% resistance=220 package=THT]
  R19 = Resistor [tolerance=±5% resistance=220 package=THT]
  R20 = Resistor [tolerance=±5% resistance=220 package=THT]
  R21 = Resistor [tolerance=±5% resistance=220 package=THT]
  R22 = Resistor [tolerance=±5% resistance=220 package=THT]
  R23 = Resistor [tolerance=±5% resistance=220 package=THT]
  R24 = Resistor [tolerance=±5% resistance=220 package=THT]
  R25 = Resistor [tolerance=±5% resistance=220 package=THT]
  R26 = Resistor [tolerance=±5% resistance=220 package=THT]
  R27 = Resistor [tolerance=±5% resistance=220 package=THT]
  R29 = Resistor [tolerance=±5% resistance=220 package=THT]
  R31 = Resistor [tolerance=±5% resistance=220 package=THT]

nets:
  N1: IC1.A14, J1.pin1
  N2: IC1.A12, J1.pin3
  N3: IC1.I/O0, J2.pin8
  N4: IC1.I/O1, J2.pin7
  N5: IC1.I/O2, J2.pin6
  GND: IC1.GND, IC2.GND
  N6: IC1.I/O3, J2.pin5
  N7: IC1.I/O4, J2.pin4
  N8: IC1.I/O5, J2.pin3
  N9: IC1.I/O6, J2.pin2
  N10: IC1.I/O7, J2.pin1
  N11: IC1._CE, IC1._OE, IC2._CE, IC2._OE
  N12: IC1.A10, J1.pin5
  N13: IC1.A11, J1.pin4
  N14: IC1.A9, J1.pin6
  N15: IC1.A8, J1.pin7
  N16: IC1.A13, J1.pin2
  VCC: IC1._WE, IC1.VCC, IC2._WE, IC2.VCC
  N17: J3.pin2, IC2.A13
  N18: J3.pin4, IC2.A11
  N19: J3.pin5, IC2.A10
  N20: J3.pin6, IC2.A9
  N21: J3.pin7, IC2.A8
  N22: IC2.I/O0, J4.pin8
  N23: IC2.I/O1, J4.pin7
  N24: IC2.I/O2, J4.pin6
  N25: IC2.I/O3, J4.pin5
  N26: IC2.I/O4, J4.pin4
  N27: IC2.I/O5, J4.pin3
  N28: IC2.I/O6, J4.pin2
  N29: IC2.I/O7, J4.pin1
  N30: J5.pin1, IC3.8Q
  N31: J5.pin2, IC3.7Q
  N32: J5.pin3, IC3.6Q
  N33: J5.pin4, IC3.5Q
  N34: J5.pin5, IC3.4Q
  N35: J5.pin6, IC3.3Q
  N36: J5.pin7, IC3.2Q
  N37: J5.pin8, IC3.1Q
  GND_2: IC3._CLKEN, IC3.GND, IC4._OE, IC4._OE2, IC4.GND, IC5.2A, IC5.3A, IC5.GND, IC6.P0, IC6.P1, IC6.P2, IC6.P3, IC6.GND
  N38: IC3.1D, J6.pin8
  N39: IC3.2D, J6.pin7
  N40: IC3.3D, J6.pin6
  N41: IC3.4D, J6.pin5
  N42: IC3.CLK, IC4.CP, IC5.1Y, IC6.CP
  N43: IC3.5D, J6.pin4
  N44: IC3.6D, J6.pin3
  N45: IC3.7D, J6.pin2
  N46: IC3.8D, J6.pin1
  VCC_2: IC3.VCC, IC4.VCC, IC5.VCC, IC6.TE, IC6.VCC
  N47: IC4._E1, IC4._E2, IC4.MR, IC5.4A, IC5.5A
  N48: IC5.1A, C/U_TIMER_RESET1.pin1, C/U_TIMER_RESET1.pin2
  N49: IC5.6Y, IC6._SPE
  N50: IC5.6A, C/U_TIMER_RESET.pin1, C/U_TIMER_RESET.pin2
  N51: IC6._MR, RESET.pin1, RESET.pin2
  N52: IC6.Q2, LED2.anode
  N53: IC6.Q1, LED3.anode
  N54: IC6.Q0, LED4.anode
  N55: IC7._G2A, IC7._G2B, IC7.GND
  N56: IC7.Y7, LED12.cathode
  N57: IC7.Y6, LED11.cathode
  N58: IC7.Y5, LED10.cathode
  N59: IC7.Y4, LED9.cathode
  N60: IC7.Y3, LED8.cathode
  N61: IC7.Y2, LED7.cathode
  N62: IC7.Y1, LED6.cathode
  N63: IC7.Y0, LED5.cathode
  N64: LED13.cathode, J8.pin4
  N65: LED14.cathode, J8.pin3
  N66: LED15.cathode, J8.pin2
  N67: LED16.cathode, J8.pin1
  N68: LED17.cathode, J7.pin1
  N69: LED18.cathode, J7.pin5
  N70: LED19.cathode, J7.pin2
  N71: LED20.cathode, J7.pin6
  N72: LED21.cathode, J7.pin7
  N73: LED22.cathode, J7.pin3
  N74: LED23.cathode, J7.pin4
  N75: LED24.cathode, J7.pin8
  N76: IC8.A14, J10.pin1
  N77: IC8.A12, J10.pin3
  N78: IC8.I/O0, J12.pin8
  N79: IC8.I/O1, J12.pin7
  N80: IC8.I/O2, J12.pin6
  GND_3: IC8.GND, IC9.GND
  N81: IC8.I/O3, J12.pin5
  N82: IC8.I/O4, J12.pin4
  N83: IC8.I/O5, J12.pin3
  N84: IC8.I/O6, J12.pin2
  N85: IC8.I/O7, J12.pin1
  N86: IC8._CE, IC8._OE, IC9._CE, IC9._OE
  N87: IC8.A10, J10.pin5
  N88: IC8.A11, J10.pin4
  N89: IC8.A9, J10.pin6
  N90: IC8.A8, J10.pin7
  N91: IC8.A13, J10.pin2
  VCC_3: IC8._WE, IC8.VCC, IC9._WE, IC9.VCC
  N92: J9.pin2, IC9.A13
  N93: J9.pin4, IC9.A11
  N94: J9.pin5, IC9.A10
  N95: J9.pin6, IC9.A9
  N96: J9.pin7, IC9.A8
  N97: J11.pin1, IC9.I/O7
  N98: J11.pin2, IC9.I/O6
  N99: J11.pin3, IC9.I/O5
  N100: J11.pin4, IC9.I/O4
  N101: J11.pin5, IC9.I/O3
  N102: J11.pin6, IC9.I/O2
  N103: J11.pin7, IC9.I/O1
  N104: J11.pin8, IC9.I/O0
  N105: LED27.cathode, J13.pin1
  N106: LED27.anode, J13.pin2
  N107: LED28.cathode, J13.pin3
  N108: LED28.anode, J13.pin4
  N109: LED29.cathode, J13.pin5
  N110: LED29.anode, J13.pin6
  N111: LED31.cathode, J13.pin7
  N112: LED31.anode, J13.pin8
  N113: LED35.cathode, J14.pin1
  N114: LED35.anode, J14.pin2
  N115: LED37.cathode, J14.pin5
  N116: LED37.anode, J14.pin6
  N117: LED38.cathode, J14.pin7
  N118: LED38.anode, J14.pin8
  N119: LED39.cathode, J14.pin3
  N120: LED39.anode, J14.pin4
  N121: LED43.cathode, J15.pin1
  N122: LED43.anode, J15.pin2
  N123: LED45.cathode, J15.pin5
  N124: LED45.anode, J15.pin6
  N125: LED46.cathode, J15.pin7
  N126: LED46.anode, J15.pin8
  N127: LED47.cathode, J15.pin3
  N128: LED47.anode, J15.pin4
  N129: LED51.cathode, J16.pin1
  N130: LED51.anode, J16.pin2
  N131: LED53.cathode, J16.pin5
  N132: LED55.cathode, J16.pin3
  N133: LED55.anode, J16.pin4
  N134: R1.Pin_0, R2.Pin_0, R3.Pin_0, R4.Pin_0, R5.Pin_0, R6.Pin_0, R7.Pin_0, R8.Pin_0, R9.Pin_0, R10.Pin_0, R11.Pin_0, R12.Pin_0, R13.Pin_0, R14.Pin_0, R15.Pin_0, R16.Pin_0, R17.Pin_0, R18.Pin_0, R19.Pin_0, R20.Pin_0, R21.Pin_0, R22.Pin_0, R23.Pin_0, R24.Pin_0, R25.Pin_0, R26.Pin_0, R27.Pin_0, R29.Pin_0, R31.Pin_0

custom parts:
  DIP - 28 pins: 256kbit EEPROM
  74HCT377: Octal D-Type flip flops with clock enable 8 bit register
  DIP - 16 pins: 4 bit register
  DIP - 14 pins: Hex Inverter
  DIP - 16 pins: 4 bit synchronous counter with load and asynchronous clear
  DIP - 16 pins: 3 to 8 decoder
