// Logisim project 8bit_74_series_computer.circ as structural Verilog: 26 circuits, main circuit main
module main (
  input  in_1,
  input  in_2,
  input  [7:0] in_3
);

  wire ALU_add_sub, ALU_output_enable, button_1_out, carry, clear, clock, CLOCK_clock, finished_user_input,
       halt, instruction_register_input_enable, INSTRUCTION_REGISTER_p1, INSTRUCTION_REGISTER_p2,
       manual_clock_pulse, memory_address_register_input_enable, program_counter_increment,
       program_counter_input_enable, program_counter_output_enable, ram_input_enable, ram_output_enable,
       register_A_input_enable, register_A_output_enable, register_B_input_enable, register_B_output_enable;
  wire [2:0] microcode_step;
  wire [7:0] A_register_contents, ALU_result, B_register_contents, bus, C_register_contents,
       D_register_contents, display_content, instruction_register_contents, memory_address_register_contents,
       program_counter_contents, stack_pointer_contents;

  Button button_1 (.out(button_1_out));
  Button button_2 (.out(clear));
  Button button_3 (.out(finished_user_input));
  or or_1 (manual_clock_pulse, in_1, button_1_out);
  // Probe on register_A_input_enable
  // Probe on register_A_output_enable
  // Probe on register_B_input_enable
  // Probe on register_B_output_enable
  // Probe on ALU_output_enable
  // Probe on ALU_add_sub
  // Probe on memory_address_register_input_enable
  // Probe on ram_input_enable
  // Probe on ram_output_enable
  // Probe on program_counter_input_enable
  // Probe on program_counter_output_enable
  // Probe on program_counter_increment
  // Probe on instruction_register_input_enable
  // Probe on halt
  // Probe on clock
  // Probe on carry
  // Probe on bus
  // Probe on program_counter_contents
  // Probe on A_register_contents
  // Probe on ALU_result
  // Probe on B_register_contents
  // Probe on memory_address_register_contents
  // Probe on instruction_register_contents
  // Probe on microcode_step
  // Probe on microcode_step
  // Probe on bus
  // Probe on program_counter_contents
  // Probe on A_register_contents
  // Probe on ALU_result
  // Probe on B_register_contents
  // Probe on memory_address_register_contents
  // Probe on instruction_register_contents
  // Probe on microcode_step
  // Probe on bus
  // Probe on program_counter_contents
  // Probe on A_register_contents
  // Probe on ALU_result
  // Probe on B_register_contents
  // Probe on memory_address_register_contents
  // Probe on instruction_register_contents
  // OR_Gate or_2 is placed but not wired
  control_unit control_unit_1 ();  // open: register_A_input_enable, register_A_output_enable, register_B_input_enable, register_B_output_enable, alu_input_enable, alu_output_enable, alu_s_3, alu_c_in, alu_m, memory_address_input_enable, memory_input_enable, memory_output_enable, program_counter_input_enable, halt, clock, clear, alu_zero, instruction, microcode_step, register_C_input_enable, register_C_output_enable, register_D_input_enable, register_D_output_enable, alu_s_0, alu_s_1, alu_s_2, alu_carry_compare, alu_equality, program_counter_output_enable, program_counter_count, stack_pointer_input_enable, stack_pointer_output_enable, instruction_register_input_enable, program_memory_select, step_counter_reset, clocked_instruction, clocked_flags, sim_only_clear
  clock u_CLOCK (
    .Reset(manual_clock_pulse), .Clock(CLOCK_clock), .Auto_Manual(in_2));  // open: Halt, Control_Clock, Manual_clock
  // register_bus_R INSTRUCTION_REGISTER: pin names not known; wires that end beside it: INSTRUCTION_REGISTER_p1, INSTRUCTION_REGISTER_p2, bus, bus, instruction_register_contents
  // program_counter PROGRAM_COUNTER: pin names not known; wires that end beside it: INSTRUCTION_REGISTER_p2, INSTRUCTION_REGISTER_p1, bus, bus, program_counter_contents
  // register_bus_R STACK_POINTER: pin names not known; wires that end beside it: INSTRUCTION_REGISTER_p1, INSTRUCTION_REGISTER_p2, bus, bus, stack_pointer_contents
  // register_bus_R A_REGISTER: pin names not known; wires that end beside it: INSTRUCTION_REGISTER_p1, INSTRUCTION_REGISTER_p2, bus, bus, A_register_contents
  // register_bus_R B_REGISTER: pin names not known; wires that end beside it: INSTRUCTION_REGISTER_p1, INSTRUCTION_REGISTER_p2, bus, bus, B_register_contents
  // register_bus_R C_REGISTER: pin names not known; wires that end beside it: INSTRUCTION_REGISTER_p1, INSTRUCTION_REGISTER_p2, bus, bus, C_register_contents
  // register_bus_R D_REGISTER: pin names not known; wires that end beside it: INSTRUCTION_REGISTER_p1, INSTRUCTION_REGISTER_p2, bus, bus, D_register_contents
  Pull_Resistor pull_resistor_1 (.node(bus));
  user_input USER_INPUT (.buffered_output(bus));  // open: user_input, output_enable
  // register_bus_L MEMORY_ADDRESS_REGISTER: pin names not known; wires that end beside it: bus, bus, memory_address_register_contents
  // RAM RAM: pin names not known; wires that end beside it: memory_address_register_contents, bus, bus
  request_user_input REQUEST_USER_INPUT (
    .\input (bus), .buffered_output(bus));  // open: user_finished, input_enable, clear, output_enable, waiting_for_user_input
  // register_bus_L DISPLAY: pin names not known; wires that end beside it: bus, bus, display_content
  memory_map_controller memory_map_controller_1 ();  // open: input_ram_input_enable, input_ram_output_enable, address, output_ram_input_enable, output_ram_output_enable, MMD_0_input_enable, MMD_0_output_enable, MMD_1_input_enable, MMD_1_output_enable, MMD_2_input_enable, MMD_2_output_enable, clock, sim_only_clear, address_clocked

  // Other names for the same wires on the sheet: auto_manual_clock = in_2; user_input[7:0] = in_3

  // Notes on the sheet:
  //   this is needed for getting rid of strange startup error condiitions in logisim
endmodule

module ALU (
  input  [7:0] A,
  input  [7:0] B,
  input  carry_in,
  input  M,
  input  S0,
  input  S1,
  input  S2,
  input  S3,
  input  output_enable,
  input  clock,
  input  store_result,
  input  store_flags,
  output unclocked_zero,
  output clocked_zero,
  output unclocked_negative,
  output clocked_negative,
  output unclocked_carry_out,
  output clocked_carry_out,
  output unclocked_A___B,
  output clocked_A___B,
  output [7:0] tristate_clocked_result,
  output [7:0] unclocked_result,
  output [7:0] clocked_result
);

  wire and_2_out, and_3_out, and_4_out, and_5_out, n74ls181_1_a_b, n74ls181_1_carry_out_bar, n74ls181_2_a_b,
       n74ls181_2_carry_out_bar, nor_1_out, nor_2_out, nor_3_out, nor_4_out, nor_5_out, nor_6_out, nor_7_out,
       nor_8_out, not_2_out, not_3_out, not_4_out, not_5_out, not_6_out;

  and and_1 (unclocked_A___B, n74ls181_1_a_b, n74ls181_2_a_b);
  not not_1 (unclocked_carry_out, n74ls181_2_carry_out_bar);
  not not_2 (not_2_out, carry_in);
  _74LS181 u_74ls181_1 (
    .B(B[3:0]), .A(A[3:0]), .M(M), .carry_in_bar(not_2_out), .carry_out_bar(n74ls181_1_carry_out_bar),
    .F(unclocked_result[3:0]), .A_B(n74ls181_1_a_b), .S0(S0), .S1(S1), .S2(S2), .S3(S3));  // open: Y, X
  _74LS181 u_74ls181_2 (
    .B(B[7:4]), .A(A[7:4]), .M(M), .carry_in_bar(n74ls181_1_carry_out_bar),
    .carry_out_bar(n74ls181_2_carry_out_bar), .F({unclocked_negative, unclocked_result[6:4]}),
    .A_B(n74ls181_2_a_b), .S0(S0), .S1(S1), .S2(S2), .S3(S3));  // open: Y, X
  not not_3 (not_3_out, store_result);
  not not_4 (not_4_out, clock);
  not not_5 (not_5_out, store_flags);
  not not_6 (not_6_out, clock);
  nor nor_1 (nor_1_out, unclocked_result[0], unclocked_result[1]);
  nor nor_2 (nor_2_out, unclocked_result[2], unclocked_result[3]);
  nor nor_3 (nor_3_out, unclocked_result[4], unclocked_result[5]);
  nor nor_4 (nor_4_out, unclocked_result[6], unclocked_negative);
  nor nor_5 (nor_5_out, not_3_out, nor_6_out);
  nor nor_6 (nor_6_out, nor_5_out, not_4_out);
  nor nor_7 (nor_7_out, not_5_out, nor_8_out);
  nor nor_8 (nor_8_out, nor_7_out, not_6_out);
  and and_2 (and_2_out, nor_1_out, nor_2_out);
  and and_3 (and_3_out, nor_3_out, nor_4_out);
  and and_4 (and_4_out, nor_5_out, clock);
  and and_5 (and_5_out, nor_7_out, clock);
  and and_6 (unclocked_zero, and_2_out, and_3_out);
  Register result (
    .D({unclocked_negative, unclocked_result[6:0]}), .en(1'b1), .Q(clocked_result), .clk(and_4_out),
    .clr(1'b0));
  assign tristate_clocked_result = output_enable ? clocked_result : 8'bz;  // Controlled_Buffer controlled_buffer_1
  Register #(.width(4)) register_1 (
    .D({unclocked_A___B, unclocked_carry_out, unclocked_negative, unclocked_zero}), .en(1'b1),
    .Q({clocked_A___B, clocked_carry_out, clocked_negative, clocked_zero}), .clk(and_5_out), .clr(1'b0));

  assign unclocked_result[7] = unclocked_negative;
endmodule

module register_bus_R (
  input  [7:0] \input ,
  input  input_enable,
  input  clock,
  input  output_enable,
  output [7:0] content,
  output [7:0] buffered_output
);

  wire and_1_out;

  Register register_1 (.D(\input ), .en(1'b1), .Q(content), .clk(and_1_out), .clr(1'b0));
  and and_1 (and_1_out, input_enable, clock);
  assign buffered_output = output_enable ? content : 8'bz;  // Controlled_Buffer controlled_buffer_1
endmodule

module register_bus_L (
  input  [7:0] \input ,
  input  input_enable,
  input  clock,
  input  output_enable,
  output [7:0] content,
  output [7:0] buffered_output
);

  wire and_1_out;

  Register register_1 (.D(\input ), .en(1'b1), .Q(content), .clk(and_1_out), .clr(1'b0));
  and and_1 (and_1_out, input_enable, clock);
  assign buffered_output = output_enable ? content : 8'bz;  // Controlled_Buffer controlled_buffer_1
endmodule

module clock (
  input  Halt,
  input  Auto_Manual,
  input  Reset,
  input  Manual_clock,
  output Clock,
  output Control_Clock
);

  wire Auto_clock_out, nand_1_out, nand_2_out, nand_3_out, nand_4_out, nand_5_out, nand_6_out, nand_7_out,
       nor_1_out, nor_2_out, nor_3_out, nor_4_out, not_1_out, not_2_out;

  Clock #(.highDuration(4), .lowDuration(4)) Auto_clock (.out(Auto_clock_out));
  nand nand_1 (nand_1_out, Auto_Manual, Auto_Manual);
  nand nand_2 (nand_2_out, Auto_Manual, Manual_clock);
  nand nand_3 (nand_3_out, nand_1_out, Auto_clock_out);
  nand nand_4 (nand_4_out, nand_2_out, nand_3_out);
  nor nor_1 (nor_1_out, nand_4_out, nand_4_out);
  nor nor_2 (nor_2_out, Halt, Reset);
  nor nor_3 (nor_3_out, Reset, nor_4_out);
  nor nor_4 (nor_4_out, nor_3_out, nor_1_out);
  nand nand_5 (nand_5_out, nor_3_out, nand_4_out);
  nand nand_6 (nand_6_out, nand_5_out, nand_5_out);
  nand nand_7 (nand_7_out, nand_6_out, nand_6_out);
  J_K_Flip_Flop j_k_ff_1 (
    .J(1'b1), .clk(nand_6_out), .K(1'b1), .Q(Clock), .preset(1'b0), .en(1'b1), .reset(not_1_out));  // open: Qn
  not not_1 (not_1_out, nor_2_out);
  J_K_Flip_Flop j_k_ff_2 (
    .J(1'b1), .clk(nand_7_out), .K(1'b1), .Q(Control_Clock), .preset(1'b0), .en(1'b1), .reset(not_2_out));  // open: Qn
  not not_2 (not_2_out, nor_2_out);
endmodule

module RAM (
  input  [7:0] \input ,
  input  input_enable,
  input  [7:0] address,
  input  Select_prog_mem,
  input  clock,
  input  output_enable,
  output [7:0] current_data,
  output [7:0] tristate_output
);

  wire not_1_out;

  RAM_part #(.addrWidth(9)) ram_1 (
    .addr({Select_prog_mem, address}), .data(current_data), .sel(1'b1), .clk(clock), .ld(not_1_out),
    .clr(1'b0));
  not not_1 (not_1_out, input_enable);
  assign current_data = input_enable ? \input  : 8'bz;  // Controlled_Buffer controlled_buffer_1
  assign tristate_output = output_enable ? current_data : 8'bz;  // Controlled_Buffer controlled_buffer_2
endmodule

module program_counter (
  input  in,
  input  output_enable,
  input  [7:0] \input ,
  input  count,
  input  clock,
  input  clear,
  output [7:0] tristate_output,
  output [7:0] contents
);

  Counter counter_1 (.load(in), .D(\input ), .count(count), .Q(contents), .clk(clock), .clr(clear));  // open: carry
  assign tristate_output = output_enable ? contents : 8'bz;  // Controlled_Buffer controlled_buffer_1
endmodule

module control_unit (
  input  [7:0] instruction,
  input  clock,
  input  clear,
  input  sim_only_clear,
  input  alu_zero,
  input  alu_carry_compare,
  input  alu_equality,
  output register_A_input_enable,
  output register_A_output_enable,
  output register_B_input_enable,
  output [7:0] clocked_instruction,
  output register_B_output_enable,
  output register_C_input_enable,
  output register_C_output_enable,
  output [2:0] microcode_step,
  output register_D_input_enable,
  output register_D_output_enable,
  output alu_input_enable,
  output alu_output_enable,
  output alu_s_0,
  output alu_s_1,
  output alu_s_2,
  output alu_s_3,
  output alu_c_in,
  output alu_m,
  output memory_address_input_enable,
  output [2:0] clocked_flags,
  output memory_input_enable,
  output memory_output_enable,
  output program_counter_input_enable,
  output program_counter_output_enable,
  output program_counter_count,
  output stack_pointer_input_enable,
  output stack_pointer_output_enable,
  output instruction_register_input_enable,
  output program_memory_select,
  output step_counter_reset,
  output halt
);

  wire not_1_out, not_2_out;
  wire [3:3] clocked_flags_q, undriven;
  wire [7:4] rom_4_data;

  Register u_clocked_instruction (
    .D(instruction), .en(1'b1), .Q(clocked_instruction), .clk(not_2_out), .clr(sim_only_clear));
  not not_1 (not_1_out, step_counter_reset);
  not not_2 (not_2_out, clock);
  Register #(.width(4)) u_clocked_flags (
    .D({undriven[3], alu_equality, alu_carry_compare, alu_zero}), .en(1'b1),
    .Q({clocked_flags_q[3], clocked_flags}), .clk(not_2_out), .clr(sim_only_clear));
  Counter #(.width(3), .max('h7)) microcode_step_counter (
    .load(step_counter_reset), .D(3'b000), .count(not_1_out), .Q(microcode_step), .clk(not_2_out), .clr(clear));  // open: carry
  ROM #(.addrWidth(15)) rom_1 (
    .addr({1'b0, clocked_flags, microcode_step, clocked_instruction}),
    .data({register_D_output_enable, register_D_input_enable, register_C_output_enable, register_C_input_enable, register_B_output_enable, register_B_input_enable, register_A_output_enable, register_A_input_enable}),
    .sel(1'b1));
  ROM #(.addrWidth(15)) rom_2 (
    .addr({1'b0, clocked_flags, microcode_step, clocked_instruction}),
    .data({alu_m, alu_c_in, alu_s_3, alu_s_2, alu_s_1, alu_s_0, alu_output_enable, alu_input_enable}),
    .sel(1'b1));
  ROM #(.addrWidth(15)) rom_3 (
    .addr({1'b0, clocked_flags, microcode_step, clocked_instruction}),
    .data({stack_pointer_output_enable, stack_pointer_input_enable, program_counter_count, program_counter_output_enable, program_counter_input_enable, memory_output_enable, memory_input_enable, memory_address_input_enable}),
    .sel(1'b1));
  ROM #(.addrWidth(15)) rom_4 (
    .addr({1'b0, clocked_flags, microcode_step, clocked_instruction}),
    .data({rom_4_data, halt, step_counter_reset, program_memory_select, instruction_register_input_enable}),
    .sel(1'b1));
  // Pins of 3 and 4 bits meet at {clocked_flags_q[3], clocked_flags}

  // Notes on the sheet:
  //   microcode 0
  //   microcode 1
  //   microcode 2
  //   microcode 3
  //   contents of rom_1 (hex, n*v repeats v):
  //   4*10 4*c 4*10 4*8 4*0 4*2 72*0 4*10 4*c 4*0 4*2 16*0 4*10 4*c 4*0 4*2 80*0 4*10 4*c 4*10 4*8 4*0 4*2
  //   200*0 4*10 4*c 8 10 8 10 2 20 2 20 0 2 0 2 108*0 4*10 4*c 4*2 20*0 4*10 4*c 4*1
  //   contents of rom_2 (hex, n*v repeats v):
  //   4*4 4*1 4*4 4*5 4*1 76*0 4*4 4*1 4*20 20*0 4*4 4*1 4*10 84*0 4*4 4*1 4*4 4*5 4*81 204*0 4*4 4*1 0 4
  //   0 4 0 1 0 1 112*0 4*4 4*1 24*0 4*4 4*1
  //   contents of rom_3 (hex, n*v repeats v):
  //   16*0 4*2 84*0 4*1 28*0 4*2
  //   contents of rom_4 (hex, n*v repeats v):
  //   16*0 4*2 84*0 4*1 28*0 4*2
endmodule

module memory_map_controller (
  input  input_ram_input_enable,
  input  input_ram_output_enable,
  input  [7:0] address,
  input  sim_only_clear,
  input  clock,
  output output_ram_input_enable,
  output output_ram_output_enable,
  output MMD_0_input_enable,
  output MMD_0_output_enable,
  output [7:0] address_clocked,
  output MMD_1_input_enable,
  output MMD_1_output_enable,
  output MMD_2_input_enable,
  output MMD_2_output_enable
);

  wire not_1_out;

  Register register_1 (.D(address), .en(1'b1), .Q(address_clocked), .clk(not_1_out), .clr(sim_only_clear));
  not not_1 (not_1_out, clock);
  ROM #(.addrWidth(10)) rom_1 (
    .addr({input_ram_input_enable, input_ram_output_enable, address_clocked}),
    .data({MMD_2_output_enable, MMD_2_input_enable, MMD_1_output_enable, MMD_1_input_enable, MMD_0_output_enable, MMD_0_input_enable, output_ram_output_enable, output_ram_input_enable}),
    .sel(1'b1));
endmodule

module request_user_input (
  input  user_finished,
  input  clear,
  input  output_enable,
  input  [7:0] \input ,
  input  input_enable,
  output waiting_for_user_input,
  output [7:0] buffered_output
);

  wire and_1_out, and_2_out, or_1_out;
  wire [0:0] not_1_out;

  and and_1 (and_1_out, waiting_for_user_input, user_finished);
  and and_2 (and_2_out, \input [0], input_enable);
  or or_1 (or_1_out, and_1_out, and_2_out);
  J_K_Flip_Flop j_k_ff_1 (
    .J(1'b1), .clk(or_1_out), .K(1'b1), .Q(waiting_for_user_input), .preset(1'b0), .en(1'b1), .reset(clear));  // open: Qn
  not not_1 (not_1_out[0], waiting_for_user_input);
  assign buffered_output = output_enable ? {{7{1'b0}}, not_1_out[0]} : 8'bz;  // Controlled_Buffer controlled_buffer_1
endmodule

module user_input (
  input  [7:0] user_input,
  input  output_enable,
  output [7:0] buffered_output
);

  assign buffered_output = output_enable ? user_input : 8'bz;  // Controlled_Buffer controlled_buffer_1
endmodule

module _74LS181 (
  input  S0,
  input  S1,
  input  S2,
  input  S3,
  input  [3:0] B,
  input  [3:0] A,
  input  M,
  input  carry_in_bar,
  output Y,
  output carry_out_bar,
  output X,
  output [3:0] F,
  output A_B
);

  wire and_1_out, and_2_out, and_3_out, and_4_out, and_5_out, and_6_out, and_7_out, and_8_out, and_9_out,
       and_10_out, and_11_out, and_12_out, and_13_out, and_14_out, and_15_out, and_16_out, and_17_out,
       and_18_out, and_19_out, and_20_out, and_21_out, and_22_out, and_23_out, and_24_out, and_25_out,
       and_26_out, and_27_out, and_28_out, nand_1_out, nand_3_out, nor_1_out, nor_2_out, nor_3_out,
       nor_4_out, nor_5_out, nor_6_out, nor_7_out, nor_8_out, nor_10_out, nor_11_out, nor_12_out, not_1_out,
       not_2_out, not_3_out, not_4_out, not_5_out, xor_1_out, xor_2_out, xor_3_out, xor_4_out;

  not not_1 (not_1_out, B[3]);
  not not_2 (not_2_out, B[2]);
  not not_3 (not_3_out, B[1]);
  not not_4 (not_4_out, B[0]);
  not not_5 (not_5_out, M);
  and and_1 (and_1_out, B[3], S3, A[3]);
  and and_2 (and_2_out, A[3], S2, not_1_out);
  and and_3 (and_3_out, not_1_out, S1);
  and and_4 (and_4_out, S0, B[3]);
  and and_5 (and_5_out, B[2], S3, A[2]);
  and and_6 (and_6_out, A[2], S2, not_2_out);
  and and_7 (and_7_out, not_2_out, S1);
  and and_8 (and_8_out, S0, B[2]);
  and and_9 (and_9_out, B[1], S3, A[1]);
  and and_10 (and_10_out, A[1], S2, not_3_out);
  and and_11 (and_11_out, not_3_out, S1);
  and and_12 (and_12_out, S0, B[1]);
  and and_13 (and_13_out, B[0], S3, A[0]);
  and and_14 (and_14_out, A[0], S2, not_4_out);
  and and_15 (and_15_out, not_4_out, S1);
  and and_16 (and_16_out, S0, B[0]);
  nor nor_1 (nor_1_out, and_1_out, and_2_out);
  nor nor_2 (nor_2_out, and_3_out, and_4_out, A[3]);
  nor nor_3 (nor_3_out, and_5_out, and_6_out);
  nor nor_4 (nor_4_out, and_7_out, and_8_out, A[2]);
  nor nor_5 (nor_5_out, and_9_out, and_10_out);
  nor nor_6 (nor_6_out, and_11_out, and_12_out, A[1]);
  nor nor_7 (nor_7_out, and_13_out, and_14_out);
  nor nor_8 (nor_8_out, and_15_out, and_16_out, A[0]);
  xor xor_1 (xor_1_out, nor_1_out, nor_2_out);
  xor xor_2 (xor_2_out, nor_3_out, nor_4_out);
  xor xor_3 (xor_3_out, nor_5_out, nor_6_out);
  xor xor_4 (xor_4_out, nor_7_out, nor_8_out);
  and and_17 (and_17_out, nor_1_out, nor_4_out);
  and and_18 (and_18_out, nor_1_out, nor_3_out, nor_6_out);
  and and_19 (and_19_out, nor_1_out, nor_3_out, nor_5_out, nor_8_out);
  nand nand_1 (nand_1_out, nor_1_out, nor_3_out, nor_5_out, nor_7_out, carry_in_bar);
  nand nand_2 (X, nor_1_out, nor_3_out, nor_5_out, nor_7_out);
  and and_20 (and_20_out, carry_in_bar, nor_7_out, nor_5_out, nor_3_out, not_5_out);
  and and_21 (and_21_out, nor_5_out, nor_3_out, nor_8_out, not_5_out);
  and and_22 (and_22_out, nor_3_out, nor_6_out, not_5_out);
  and and_23 (and_23_out, nor_4_out, not_5_out);
  and and_24 (and_24_out, carry_in_bar, nor_7_out, nor_5_out, not_5_out);
  and and_25 (and_25_out, nor_5_out, nor_8_out, not_5_out);
  and and_26 (and_26_out, nor_6_out, not_5_out);
  and and_27 (and_27_out, carry_in_bar, nor_7_out, not_5_out);
  and and_28 (and_28_out, nor_8_out, not_5_out);
  nand nand_3 (nand_3_out, carry_in_bar, not_5_out);
  nor nor_9 (Y, nor_2_out, and_17_out, and_18_out, and_19_out);
  nor nor_10 (nor_10_out, and_20_out, and_21_out, and_22_out, and_23_out);
  nor nor_11 (nor_11_out, and_24_out, and_25_out, and_26_out);
  nor nor_12 (nor_12_out, and_27_out, and_28_out);
  or or_1 (carry_out_bar, ~Y, ~nand_1_out);  // OR_Gate
  xor xor_5 (F[3], xor_1_out, nor_10_out);
  xor xor_6 (F[2], xor_2_out, nor_11_out);
  xor xor_7 (F[1], xor_3_out, nor_12_out);
  xor xor_8 (F[0], xor_4_out, nand_3_out);
  and and_29 (A_B, F[3], F[2], F[1], F[0]);
endmodule

module test_74LS181 (
  input  [3:0] in_1,
  input  [3:0] in_2,
  input  in_3,
  input  in_4,
  input  in_5,
  input  in_6,
  input  in_7,
  input  in_8,
  input  [7:0] in_9,
  input  [7:0] in_10,
  input  in_11,
  input  in_12,
  input  in_13,
  input  in_14,
  input  in_15,
  input  in_16,
  output out_17,
  output out_18,
  output out_19,
  output out_20,
  output out_21,
  output out_22
);

  wire n74ls181_2_a_b, n74ls181_2_carry_out_bar, n74ls181_3_a_b;
  wire [3:0] n74ls181_1_f, n74ls181_2_f, n74ls181_3_f;

  and and_1 (out_21, n74ls181_2_a_b, n74ls181_3_a_b);
  _74LS181 u_74ls181_1 (
    .B(in_2), .A(in_1), .M(in_4), .carry_in_bar(in_3), .Y(out_18), .carry_out_bar(out_20), .X(out_19),
    .F(n74ls181_1_f), .A_B(out_17), .S0(in_5), .S1(in_6), .S2(in_7), .S3(in_8));
  _74LS181 u_74ls181_2 (
    .B(in_10[3:0]), .A(in_9[3:0]), .M(in_12), .carry_in_bar(in_11), .carry_out_bar(n74ls181_2_carry_out_bar),
    .F(n74ls181_2_f), .A_B(n74ls181_2_a_b), .S0(in_13), .S1(in_14), .S2(in_15), .S3(in_16));  // open: Y, X
  _74LS181 u_74ls181_3 (
    .B(in_10[7:4]), .A(in_9[7:4]), .M(in_12), .carry_in_bar(n74ls181_2_carry_out_bar),
    .carry_out_bar(out_22), .F(n74ls181_3_f), .A_B(n74ls181_3_a_b), .S0(in_13), .S1(in_14), .S2(in_15),
    .S3(in_16));  // open: Y, X
  // Probe on in_1
  // Probe on in_1
  // Probe on in_1
  // Probe on in_2
  // Probe on in_2
  // Probe on in_2
  // Probe on n74ls181_1_f
  // Probe on n74ls181_1_f
  // Probe on n74ls181_1_f
  // Probe on in_9
  // Probe on in_9
  // Probe on in_9
  // Probe on in_10
  // Probe on in_10
  // Probe on in_10
  // Probe on {n74ls181_3_f, n74ls181_2_f}
  // Probe on {n74ls181_3_f, n74ls181_2_f}
  // Probe on {n74ls181_3_f, n74ls181_2_f}
endmodule

module \xor  (
  input  enable,
  input  [7:0] A_input,
  input  [7:0] B_input,
  output [7:0] buffered_output,
  output [7:0] \output 
);

  assign \output  = A_input ^ B_input;  // XOR_Gate xor_1, 8 bits wide
  assign buffered_output = enable ? \output  : 8'bz;  // Controlled_Buffer controlled_buffer_1
endmodule

module \not  (
  input  enable,
  input  [7:0] \input ,
  output [7:0] buffered_output,
  output [7:0] \output 
);

  assign \output  = ~\input ;  // NOT_Gate not_1, 8 bits wide
  assign buffered_output = enable ? \output  : 8'bz;  // Controlled_Buffer controlled_buffer_1
endmodule

module \or  (
  input  enable,
  input  [7:0] A_input,
  input  [7:0] B_input,
  output [7:0] buffered_output,
  output [7:0] \output 
);

  assign \output  = A_input | B_input;  // OR_Gate or_1, 8 bits wide
  assign buffered_output = enable ? \output  : 8'bz;  // Controlled_Buffer controlled_buffer_1
endmodule

module \and  (
  input  enable,
  input  [7:0] A_input,
  input  [7:0] B_input,
  output [7:0] buffered_output,
  output [7:0] \output 
);

  assign \output  = A_input & B_input;  // AND_Gate and_1, 8 bits wide
  assign buffered_output = enable ? \output  : 8'bz;  // Controlled_Buffer controlled_buffer_1
endmodule

module bit_shift_right (
  input  [7:0] \input ,
  input  enable,
  output [7:0] \output ,
  output [7:0] buffered_output,
  output overflow
);

  and and_1 (overflow, \input [0], enable);
  assign buffered_output = enable ? {1'b0, \input [7:1]} : 8'bz;  // Controlled_Buffer controlled_buffer_1

  assign \output  = {1'b0, \input [7:1]};
endmodule

module bit_shift_left (
  input  [7:0] \input ,
  input  enable,
  output [7:0] \output ,
  output [7:0] buffered_output,
  output overflow
);

  and and_1 (overflow, \input [7], enable);
  assign buffered_output = enable ? {\input [6:0], 1'b0} : 8'bz;  // Controlled_Buffer controlled_buffer_1

  assign \output  = {\input [6:0], 1'b0};
endmodule

module adder_subtractor (
  input  [7:0] A_input,
  input  enable,
  input  add_sub,
  input  [7:0] B_input,
  output [7:0] buffered_output,
  output [7:0] unbuffered_output,
  output carry_out
);

  wire adder_1_cout;
  wire [7:0] xor_1_out;

  assign xor_1_out = {8{add_sub}} ^ B_input;  // XOR_Gate xor_1, 8 bits wide
  Adder adder_1 (.a(A_input), .b(xor_1_out), .out(unbuffered_output), .cin(add_sub), .cout(adder_1_cout));
  and and_1 (carry_out, adder_1_cout, enable);
  assign buffered_output = enable ? unbuffered_output : 8'bz;  // Controlled_Buffer controlled_buffer_1
endmodule

module zero_check (
  input  [7:0] \input ,
  input  enable,
  output is_zero
);

  wire nor_1_out;

  nor nor_1 (nor_1_out, \input [0], \input [1], \input [2], \input [3], \input [4], \input [5], \input [6], \input [7]);
  and and_1 (is_zero, nor_1_out, enable);
endmodule

module ALU_old (
  input  [3:0] operation,
  input  [7:0] A_input,
  input  [7:0] B_input,
  input  output_enable,
  output signal,
  output [7:0] buffered_output
);

  wire adder_subtractor_1_carry_out, bit_shift_left_1_overflow, bit_shift_right_1_overflow, decoder_1_out0,
       decoder_1_out1, decoder_1_out2, decoder_1_out3, decoder_1_out4, or_1_out, or_2_out,
       zero_check_1_is_zero;
  wire [7:0] adder_subtractor_1_buffered_output, adder_subtractor_1_unbuffered_output,
       bit_shift_left_1_output, buffer_1_out, buffer_2_out;

  Decoder #(.select(4)) decoder_1 (
    .out0(decoder_1_out0), .out1(decoder_1_out1), .out2(decoder_1_out2), .out3(decoder_1_out3),
    .out4(decoder_1_out4), .sel(operation), .en(1'b1));  // open: out5, out6, out7, out8, out9, out10, out11, out12, out13, out14, out15
  or or_1 (or_1_out, decoder_1_out2, decoder_1_out1);
  or or_2 (or_2_out, bit_shift_right_1_overflow, bit_shift_left_1_overflow, adder_subtractor_1_carry_out, zero_check_1_is_zero);
  zero_check zero_check_1 (.\input (buffer_1_out), .is_zero(zero_check_1_is_zero), .enable(decoder_1_out0));
  adder_subtractor adder_subtractor_1 (
    .add_sub(decoder_1_out2), .buffered_output(adder_subtractor_1_buffered_output), .A_input(buffer_1_out),
    .enable(or_1_out), .B_input(buffer_2_out), .carry_out(adder_subtractor_1_carry_out),
    .unbuffered_output(adder_subtractor_1_unbuffered_output));
  bit_shift_left bit_shift_left_1 (
    .\input (buffer_1_out), .\output (bit_shift_left_1_output),
    .buffered_output(adder_subtractor_1_buffered_output), .overflow(bit_shift_left_1_overflow),
    .enable(decoder_1_out3));
  bit_shift_right bit_shift_right_1 (
    .\input (buffer_1_out), .buffered_output(adder_subtractor_1_buffered_output),
    .overflow(bit_shift_right_1_overflow), .enable(decoder_1_out4));  // open: output
  \and  and_1 ();  // open: A_input, B_input, buffered_output, enable, output
  \or  or_3 ();  // open: enable, A_input, buffered_output, B_input, output
  \not  not_1 ();  // open: buffered_output, input, enable, output
  \xor  xor_1 ();  // open: enable, A_input, buffered_output, B_input, output
  assign buffer_1_out = A_input;  // Buffer buffer_1, 8 bits wide
  assign buffer_2_out = B_input;  // Buffer buffer_2, 8 bits wide
  assign buffered_output = output_enable ? adder_subtractor_1_buffered_output : 8'bz;  // Controlled_Buffer controlled_buffer_1
endmodule

module ALU_test (
  input  in_1,
  input  [7:0] in_2,
  input  in_3,
  input  [7:0] in_4,
  input  in_5,
  input  in_6,
  input  in_7,
  input  in_8,
  input  in_9,
  input  in_10,
  input  in_11,
  input  in_12,
  output [7:0] out_13,
  output [7:0] out_14,
  output [7:0] out_15,
  output out_16,
  output out_17,
  output out_18,
  output out_19,
  output out_20,
  output out_21
);

  // ALU alu_1: pin names not known; wires that end beside it: in_2, out_13, out_14, out_15, out_16, out_17, out_18, out_19, out_20, out_21, in_4, in_4, in_4
  // Probe on in_2
  // Probe on in_2
  // Probe on in_4
  // Probe on in_4
  // Probe on out_15
  // Probe on out_15

  // Other names for the same wires on the sheet: A[7:0] = in_2; B[7:0] = in_4; res[7:0] = out_15
endmodule

module test (
  input  in_1,
  input  in_2,
  input  in_3,
  input  in_4,
  input  [7:0] in_5,
  input  in_6,
  input  [7:0] in_7,
  input  in_8,
  input  in_9,
  input  in_10,
  input  in_11,
  input  in_12,
  input  in_13
);

  wire [7:0] n2_to_1_io_r_1_b_2, program_counter_1_contents, program_counter_2_contents, pull_resistor_1_node;

  _2_to_1_IO_R u_2_to_1_io_r_1 (.A(in_5), .B(in_7), .A_B(in_4), .B_2(n2_to_1_io_r_1_b_2));
  // Probe on n2_to_1_io_r_1_b_2
  // Probe on pull_resistor_1_node
  Pull_Resistor pull_resistor_1 (.node(pull_resistor_1_node));
  program_counter program_counter_1 (
    .\input (pull_resistor_1_node), .count(in_3), .clock(in_6), .output_enable(in_2),
    .tristate_output(pull_resistor_1_node), .in(in_1), .contents(program_counter_1_contents), .clear(in_8));
  program_counter program_counter_2 (
    .\input (pull_resistor_1_node), .count(in_11), .clock(in_12), .output_enable(in_10),
    .tristate_output(pull_resistor_1_node), .in(in_9), .contents(program_counter_2_contents), .clear(in_13));
  // Probe on program_counter_1_contents
  // Probe on program_counter_2_contents
endmodule

module _2_to_1_IO_R (
  input  [7:0] A,
  input  [7:0] B,
  input  A_B,
  output [7:0] B_2
);

  Multiplexer #(.width(8)) multiplexer_1 (.in0(A), .in1(B), .out(B_2), .sel(A_B), .en(1'b1));
endmodule

module _2_to_1_IO_L (
  input  [7:0] A,
  input  [7:0] B,
  input  A_B,
  output [7:0] B_2
);

  Multiplexer #(.width(8)) multiplexer_1 (.in0(A), .in1(B), .out(B_2), .sel(A_B), .en(1'b1));
endmodule
